# Fritzing sketch arduino_nrf2401l+ (saved by Fritzing 0.9.3b)

parts:
  Part1 = Arduino Pro Mini (3.3V)
  Part2 = NRF24L01+ Breakout Board
  Part3 = FTDI Basic Programmer

nets:
  N1: Part1.TXO, Part3.RXI
  N2: Part1.RXI, Part3.TXO
  VCC: Part1.VCC, Part2.VCC, Part3.POWER
  GND: Part1.GND, Part2.GND, Part3.DTR, Part3.GND
  N3: Part1.SCK, Part2.SCK
  N4: Part1.MISO, Part2.MISO
  N5: Part1.MOSI, Part2.MOSI
  N6: Part1.D8, Part2.CS
  N7: Part1.D7, Part2.CE
